# Fritzing sketch muziq3 (saved by Fritzing 0.7.11b)
breadboards: 1

parts:
  Arduino1 = Arduino
  R1 = Rotary Potentiometer (Small) [maximum_resistance=100kΩ]
  R2 = Slide Potentiometer [maximum_resistance=100kΩ]
  SPKR1 = Loudspeaker
  S1 = Toggle Switch [package=THT]
  R3 = Rotary Potentiometer (Small) [maximum_resistance=100kΩ]  # not connected

nets:
  N1: Arduino1.D8, S1.L1
  N2: Arduino1.+5V, R1.leg1
  N3: Arduino1.GND, R1.leg2
  N4: Arduino1.A2, R1.wiper
  N5: R2.leg1, SPKR1.pin2
  N6: R2.leg2, S1.L2

notes:
  Volume control
  Switch to
  stop the music
